# Fritzing sketch diagrama (saved by Fritzing 0.9.3b)
breadboards: 1

parts:
  Componente2 = Arduino Uno (Rev3)
  U2 = HC-SR04 [chip_label=IC package="SIP (Single Inline) [THT]"]
  U3 = HC-SR04 [chip_label=IC package="SIP (Single Inline) [THT]"]

nets:
  N1: Componente2.D9_PWM, U3.Echo
  N2: Componente2.D10_PWM/SS, U3.Trig
  N3: Componente2.D11_PWM/MOSI, U2.Echo
  N4: Componente2.D12/MISO, U2.Trig

custom parts:
  HC-SR04: HC-SR04 ultrasound distance sensor
